// Logisim project cpu.circ as structural Verilog: 3 circuits, main circuit main
module main (
  input  [3:0] ALU_op,
  input  [1:0] B_src,
  input  C_write,
  input  data_src,
  input  [1:0] addr_src,
  input  [1:0] ACCUM_src,
  input  IR_write,
  input  PC_write,
  input  mem_write,
  input  X_src,
  input  ACCUM_write,
  input  oper_hi_write,
  input  oper_lo_write,
  input  X_write
);

  wire alu_1_c_out, alu_1_n, alu_1_v, alu_1_z, CLOCK_out, d_ff_1_q, not_1_out;
  wire [7:0] ACCUM_q, alu_1_result, IR_q, multiplexer_1_out, multiplexer_3_out, multiplexer_4_out,
       multiplexer_5_out, ram_1_data, STATE_q, X_q;
  wire [15:0] adder_1_out, adder_2_out, bit_extender_1_out, multiplexer_2_out, OPER_LO_q, PC_q, rom_1_data;

  Clock CLOCK (.out(CLOCK_out));
  assign bit_extender_1_out = {{8{1'b0}}, X_q};  // Bit_Extender bit_extender_1
  Adder #(.width(16)) adder_1 (.a(PC_q), .b(16'h1), .out(adder_1_out));  // open: cin, cout
  Register #(.width(16)) PC (.D(adder_1_out), .en(PC_write), .Q(PC_q), .clk(CLOCK_out));  // open: clr
  Adder #(.width(16)) adder_2 (.a(OPER_LO_q), .b(bit_extender_1_out), .out(adder_2_out));  // open: cin, cout
  Register STATE (.Q(STATE_q), .clk(CLOCK_out));  // open: D, en, clr
  Multiplexer #(.width(8)) multiplexer_1 (.in0(ACCUM_q), .in1(alu_1_result), .out(multiplexer_1_out), .sel(data_src));
  Multiplexer #(.select(2), .width(16)) multiplexer_2 (
    .in0(PC_q), .in1(OPER_LO_q), .in2(adder_2_out), .out(multiplexer_2_out), .sel(addr_src));  // open: in3
  RAM #(.addrWidth(16), .bus("separate")) ram_1 (
    .addr(multiplexer_2_out), .din(multiplexer_1_out), .data(ram_1_data), .str(mem_write), .clk(CLOCK_out),
    .ld(not_1_out));  // open: sel, clr
  not not_1 (not_1_out, mem_write);
  ROM #(.dataWidth(16)) rom_1 (.addr(STATE_q), .data(rom_1_data));  // open: sel
  Multiplexer #(.select(2), .width(8)) multiplexer_3 (
    .in0({8{1'b0}}), .in1(8'h1), .in2(OPER_LO_q[7:0]), .out(multiplexer_3_out), .sel(B_src));  // open: in3
  Register OPER_HI (.D(ram_1_data), .en(oper_hi_write), .Q(OPER_LO_q[15:8]), .clk(CLOCK_out));  // open: clr
  Register OPER_LO (.D(ram_1_data), .en(oper_lo_write), .Q(OPER_LO_q[7:0]), .clk(CLOCK_out));  // open: clr
  alu alu_1 (
    .oper(ALU_op), .A(ACCUM_q), .B(multiplexer_3_out), .C_in(d_ff_1_q), .Z(alu_1_z), .Result(alu_1_result),
    .C_out(alu_1_c_out), .N(alu_1_n), .V(alu_1_v));
  Multiplexer #(.width(8)) multiplexer_4 (.in0(ram_1_data), .in1(ACCUM_q), .out(multiplexer_4_out), .sel(X_src));
  Register IR (.D(ram_1_data), .en(IR_write), .Q(IR_q), .clk(CLOCK_out));  // open: clr
  Register X (.D(multiplexer_4_out), .en(X_write), .Q(X_q), .clk(CLOCK_out));  // open: clr
  Multiplexer #(.select(2), .width(8)) multiplexer_5 (
    .in0(ram_1_data), .in1(alu_1_result), .in2(X_q), .out(multiplexer_5_out), .sel(ACCUM_src));  // open: in3
  Register ACCUM (.D(multiplexer_5_out), .en(ACCUM_write), .Q(ACCUM_q), .clk(CLOCK_out));  // open: clr
  D_Flip_Flop d_ff_1 (.clk(CLOCK_out), .D(alu_1_c_out), .Q(d_ff_1_q), .en(C_write));  // open: Qn, preset, reset

  // Notes on the sheet:
  //   contents of rom_1 (hex, n*v repeats v):
  //   c000
endmodule

module alu (
  input  [3:0] oper,
  input  [7:0] A,
  input  [7:0] B,
  input  C_in,
  output Z,
  output [7:0] Result,
  output C_out,
  output N,
  output V
);

  wire adder_1_cout, subtractor_1_bout;
  wire [7:0] adder_1_out, subtractor_1_out;

  Adder adder_1 (.a(B), .b(A), .out(adder_1_out), .cin(C_in), .cout(adder_1_cout));
  Subtractor subtractor_1 (.a(A), .b(B), .out(subtractor_1_out), .bin(C_in), .bout(subtractor_1_bout));
  Multiplexer #(.select(4), .width(8)) multiplexer_1 (
    .in0(adder_1_out), .in1(subtractor_1_out), .out({N, Result[6:0]}), .sel(oper));  // open: in2, in3, in4, in5, in6, in7, in8, in9, in10, in11, in12, in13, in14, in15
  Multiplexer #(.select(4)) multiplexer_2 (
    .in0(adder_1_cout), .in1(subtractor_1_bout), .out(C_out), .sel(oper));  // open: in2, in3, in4, in5, in6, in7, in8, in9, in10, in11, in12, in13, in14, in15
  Pull_Resistor pull_resistor_1 (.node({N, Result[6:0]}));
  nor nor_1 (Z, Result[0], Result[1], Result[2], Result[3], Result[4], Result[5], Result[6], N);
  Pull_Resistor pull_resistor_2 (.node(C_out));
  overflow overflow_1 (.a(A[7]), .b(B[7]), .r(N), .v(V));
  Pull_Resistor pull_resistor_3 (.node(V));

  assign Result[7] = N;

  // Notes on the sheet:
  //   add adc, sbc and disable carry for add and sub
endmodule

module overflow (
  input  a,
  input  b,
  input  r,
  output v
);

  wire and_1_out, and_2_out, and_3_out, and_4_out, not_1_out, not_2_out, not_3_out;

  not not_1 (not_1_out, a);
  not not_2 (not_2_out, b);
  and and_1 (and_1_out, not_1_out, not_2_out);
  and and_2 (and_2_out, a, b);
  not not_3 (not_3_out, r);
  and and_3 (and_3_out, and_1_out, r);
  and and_4 (and_4_out, and_2_out, not_3_out);
  or or_1 (v, and_3_out, and_4_out);
endmodule
